// Logisim project CPU.circ as structural Verilog: 6 circuits, main circuit main
module main (
  input  RESET
);

  wire alu_1_zero, and_1_out, CLK_out, comparator_1_eq, comparator_2_eq, comparator_3_eq, comparator_4_eq,
       controlled_buffer_1_out, decode_1_jmp_stall, nand_1_out, not_1_out, not_2_out, not_3_out, or_1_out,
       xnor_1_out;
  wire [2:0] decode_1_control_lines;
  wire [3:0] s_r_ff_1_q;
  wire [4:0] decode_1_addr_in, decode_1_addr_out1, decode_1_addr_out2;
  wire [6:0] keyboard_1_data;
  wire [7:0] decode_1_imm_2;
  wire [8:3] decode_1_control_lines_2;
  wire [15:0] data_memory_1_keyboard_clr;
  wire [31:0] alu_1_s, bit_extender_1_out, data_memory_1_data_out, decode_1_imm, multiplexer_1_out,
       multiplexer_2_out, program_memory_1_instruction, registers_1_data_out1, registers_1_data_out2;
  wire [63:0] data_memory_1_screen1, data_memory_1_screen2, data_memory_1_screen3, data_memory_1_screen4;

  Clock CLK (.out(CLK_out));
  not not_1 (not_1_out, decode_1_control_lines_2[7]);
  assign controlled_buffer_1_out = not_1_out ? decode_1_jmp_stall : 1'bz;  // Controlled_Buffer controlled_buffer_1
  Program_Memory program_memory_1 (
    .Clk(CLK_out), .Rst(RESET), .Stall(controlled_buffer_1_out), .Jmp(and_1_out),
    .Jmp_Offset(decode_1_imm_2), .Instruction(program_memory_1_instruction));
  and and_1 (and_1_out, xnor_1_out, decode_1_control_lines_2[7]);
  xnor xnor_1 (xnor_1_out, alu_1_zero, decode_1_control_lines_2[8]);
  Decode decode_1 (
    .Instruction(program_memory_1_instruction), .Clk(CLK_out), .Rst(RESET), .Jmp_Stall(decode_1_jmp_stall),
    .Control_Lines({decode_1_control_lines_2, decode_1_control_lines}),
    .Imm({decode_1_imm[31:10], decode_1_imm_2, decode_1_imm[1:0]}), .Addr_Out2(decode_1_addr_out2),
    .Addr_Out1(decode_1_addr_out1), .Addr_in(decode_1_addr_in));
  not not_2 (not_2_out, decode_1_control_lines_2[3]);
  Registers registers_1 (
    .Addr_out2(decode_1_addr_out2), .Addr_out1(decode_1_addr_out1), .Data_in(multiplexer_2_out),
    .Addr_in(decode_1_addr_in), .Clk(CLK_out), .Reset(RESET), .Data_out2(registers_1_data_out2),
    .Data_out1(registers_1_data_out1));
  Multiplexer #(.width(32)) multiplexer_1 (
    .in0({decode_1_imm[31:10], decode_1_imm_2, decode_1_imm[1:0]}), .in1(registers_1_data_out2),
    .out(multiplexer_1_out), .sel(not_2_out));
  Multiplexer #(.width(32)) multiplexer_2 (
    .in0(data_memory_1_data_out), .in1(alu_1_s), .out(multiplexer_2_out), .sel(nand_1_out));
  not not_3 (not_3_out, decode_1_control_lines_2[4]);
  nand nand_1 (nand_1_out, not_3_out, decode_1_control_lines_2[5]);
  ALU alu_1 (
    .OpCode(decode_1_control_lines), .OP1(multiplexer_1_out), .OP2(registers_1_data_out1), .S(alu_1_s),
    .Zero(alu_1_zero));
  Keyboard keyboard_1 (.clk(CLK_out), .data(keyboard_1_data));  // open: re, clr, avail
  _7_Segment_Display u_7_segment_display_1 ();  // open: g, f, a, b, e, d, c, dp
  DotMatrix #(.matrixcols(16), .matrixrows(16)) dotmatrix_1 (
    .col0(data_memory_1_screen4[63:48]), .col1(data_memory_1_screen4[47:32]),
    .col2(data_memory_1_screen4[31:16]), .col3(data_memory_1_screen4[15:0]),
    .col4(data_memory_1_screen3[63:48]), .col5(data_memory_1_screen3[47:32]),
    .col6(data_memory_1_screen3[31:16]), .col7(data_memory_1_screen3[15:0]),
    .col8(data_memory_1_screen2[63:48]), .col9(data_memory_1_screen2[47:32]),
    .col10(data_memory_1_screen2[31:16]), .col11(data_memory_1_screen2[15:0]),
    .col12(data_memory_1_screen1[63:48]), .col13(data_memory_1_screen1[47:32]),
    .col14(data_memory_1_screen1[31:16]), .col15(data_memory_1_screen1[15:0]));
  Data_Memory data_memory_1 (
    .Addr(alu_1_s[9:2]), .Enable(decode_1_control_lines_2[5]), .Read_Write(decode_1_control_lines_2[4]),
    .Data_In(registers_1_data_out2), .Clk(CLK_out), .Rst(RESET), .Keyboard_In(bit_extender_1_out),
    .Data_Out(data_memory_1_data_out), .Screen3(data_memory_1_screen3), .Screen4(data_memory_1_screen4),
    .Keyboard_Clr(data_memory_1_keyboard_clr), .Screen1(data_memory_1_screen1),
    .Screen2(data_memory_1_screen2));
  or or_1 (or_1_out, data_memory_1_keyboard_clr[0], RESET);
  _7_Segment_Display u_7_segment_display_2 ();  // open: g, f, a, b, e, d, c, dp
  Comparator #(.width(7)) comparator_1 (.a(keyboard_1_data), .b(7'b1101111), .eq(comparator_1_eq));  // open: gt, lt
  Comparator #(.width(7)) comparator_2 (.a(keyboard_1_data), .b(7'b1101100), .eq(comparator_2_eq));  // open: gt, lt
  Comparator #(.width(7)) comparator_3 (.a(keyboard_1_data), .b(7'b1110111), .eq(comparator_3_eq));  // open: gt, lt
  Comparator #(.width(7)) comparator_4 (.a(keyboard_1_data), .b(7'b1110011), .eq(comparator_4_eq));  // open: gt, lt
  S_R_Flip_Flop s_r_ff_1 (
    .S(comparator_1_eq), .R(or_1_out), .clk(CLK_out), .Q(s_r_ff_1_q[0]), .reset(or_1_out));  // open: Qn, preset
  S_R_Flip_Flop s_r_ff_2 (
    .S(comparator_2_eq), .R(or_1_out), .clk(CLK_out), .Q(s_r_ff_1_q[1]), .reset(or_1_out));  // open: Qn, preset
  S_R_Flip_Flop s_r_ff_3 (
    .S(comparator_3_eq), .R(or_1_out), .clk(CLK_out), .Q(s_r_ff_1_q[2]), .reset(or_1_out));  // open: Qn, preset
  S_R_Flip_Flop s_r_ff_4 (
    .S(comparator_4_eq), .R(or_1_out), .clk(CLK_out), .Q(s_r_ff_1_q[3]), .reset(or_1_out));  // open: Qn, preset
  assign bit_extender_1_out = {{28{1'b0}}, s_r_ff_1_q};  // Bit_Extender bit_extender_1
endmodule

module Registers (
  input  [4:0] Addr_out2,
  input  [4:0] Addr_out1,
  input  [31:0] Data_in,
  input  [4:0] Addr_in,
  input  Clk,
  input  Reset,
  output [31:0] Data_out2,
  output [31:0] Data_out1
);

  wire decoder_1_out1, decoder_1_out2, decoder_1_out3, decoder_1_out4, decoder_1_out5, decoder_1_out6,
       decoder_1_out7, decoder_1_out8, decoder_1_out9, decoder_1_out10, decoder_1_out11, decoder_1_out12,
       decoder_1_out13, decoder_1_out14, decoder_1_out15, decoder_1_out16, decoder_1_out17, decoder_1_out18,
       decoder_1_out19, decoder_1_out20, decoder_1_out21, decoder_1_out22, decoder_1_out23, decoder_1_out24,
       decoder_1_out25, decoder_1_out26, decoder_1_out27, decoder_1_out28, decoder_1_out29, decoder_1_out30,
       decoder_1_out31;
  wire [31:0] x1_q, x2_q, x3_q, x4_q, x5_q, x6_q, x7_q, x8_q, x9_q, x10_q, x11_q, x12_q, x13_q, x14_q, x15_q,
       x16_q, x17_q, x18_q, x19_q, x20_q, x21_q, x22_q, x23_q, x24_q, x25_q, x26_q, x27_q, x28_q, x29_q,
       x30_q, x31_q;

  Decoder #(.select(5)) decoder_1 (
    .out1(decoder_1_out1), .out2(decoder_1_out2), .out3(decoder_1_out3), .out4(decoder_1_out4),
    .out5(decoder_1_out5), .out6(decoder_1_out6), .out7(decoder_1_out7), .out8(decoder_1_out8),
    .out9(decoder_1_out9), .out10(decoder_1_out10), .out11(decoder_1_out11), .out12(decoder_1_out12),
    .out13(decoder_1_out13), .out14(decoder_1_out14), .out15(decoder_1_out15), .out16(decoder_1_out16),
    .out17(decoder_1_out17), .out18(decoder_1_out18), .out19(decoder_1_out19), .out20(decoder_1_out20),
    .out21(decoder_1_out21), .out22(decoder_1_out22), .out23(decoder_1_out23), .out24(decoder_1_out24),
    .out25(decoder_1_out25), .out26(decoder_1_out26), .out27(decoder_1_out27), .out28(decoder_1_out28),
    .out29(decoder_1_out29), .out30(decoder_1_out30), .out31(decoder_1_out31), .sel(Addr_in), .en(1'b1));  // open: out0
  Register #(.trigger("falling"), .width(32)) x31 (
    .D(Data_in), .en(decoder_1_out31), .clk(Clk), .Q(x31_q), .clr(Reset));
  Register #(.trigger("falling"), .width(32)) x30 (
    .D(Data_in), .en(decoder_1_out30), .clk(Clk), .Q(x30_q), .clr(Reset));
  Register #(.trigger("falling"), .width(32)) x29 (
    .D(Data_in), .en(decoder_1_out29), .clk(Clk), .Q(x29_q), .clr(Reset));
  Register #(.trigger("falling"), .width(32)) x28 (
    .D(Data_in), .en(decoder_1_out28), .clk(Clk), .Q(x28_q), .clr(Reset));
  Register #(.trigger("falling"), .width(32)) x27 (
    .D(Data_in), .en(decoder_1_out27), .clk(Clk), .Q(x27_q), .clr(Reset));
  Register #(.trigger("falling"), .width(32)) x26 (
    .D(Data_in), .en(decoder_1_out26), .clk(Clk), .Q(x26_q), .clr(Reset));
  Register #(.trigger("falling"), .width(32)) x25 (
    .D(Data_in), .en(decoder_1_out25), .clk(Clk), .Q(x25_q), .clr(Reset));
  Register #(.trigger("falling"), .width(32)) x24 (
    .D(Data_in), .en(decoder_1_out24), .clk(Clk), .Q(x24_q), .clr(Reset));
  Register #(.trigger("falling"), .width(32)) x23 (
    .D(Data_in), .en(decoder_1_out23), .clk(Clk), .Q(x23_q), .clr(Reset));
  Register #(.trigger("falling"), .width(32)) x22 (
    .D(Data_in), .en(decoder_1_out22), .clk(Clk), .Q(x22_q), .clr(Reset));
  Register #(.trigger("falling"), .width(32)) x21 (
    .D(Data_in), .en(decoder_1_out21), .clk(Clk), .Q(x21_q), .clr(Reset));
  Register #(.trigger("falling"), .width(32)) x20 (
    .D(Data_in), .en(decoder_1_out20), .clk(Clk), .Q(x20_q), .clr(Reset));
  Register #(.trigger("falling"), .width(32)) x19 (
    .D(Data_in), .en(decoder_1_out19), .clk(Clk), .Q(x19_q), .clr(Reset));
  Register #(.trigger("falling"), .width(32)) x18 (
    .D(Data_in), .en(decoder_1_out18), .clk(Clk), .Q(x18_q), .clr(Reset));
  Register #(.trigger("falling"), .width(32)) x17 (
    .D(Data_in), .en(decoder_1_out17), .clk(Clk), .Q(x17_q), .clr(Reset));
  Register #(.trigger("falling"), .width(32)) x16 (
    .D(Data_in), .en(decoder_1_out16), .clk(Clk), .Q(x16_q), .clr(Reset));
  Register #(.trigger("falling"), .width(32)) x15 (
    .D(Data_in), .en(decoder_1_out15), .clk(Clk), .Q(x15_q), .clr(Reset));
  Register #(.trigger("falling"), .width(32)) x14 (
    .D(Data_in), .en(decoder_1_out14), .clk(Clk), .Q(x14_q), .clr(Reset));
  Register #(.trigger("falling"), .width(32)) x13 (
    .D(Data_in), .en(decoder_1_out13), .clk(Clk), .Q(x13_q), .clr(Reset));
  Register #(.trigger("falling"), .width(32)) x12 (
    .D(Data_in), .en(decoder_1_out12), .clk(Clk), .Q(x12_q), .clr(Reset));
  Register #(.trigger("falling"), .width(32)) x11 (
    .D(Data_in), .en(decoder_1_out11), .clk(Clk), .Q(x11_q), .clr(Reset));
  Register #(.trigger("falling"), .width(32)) x10 (
    .D(Data_in), .en(decoder_1_out10), .clk(Clk), .Q(x10_q), .clr(Reset));
  Register #(.trigger("falling"), .width(32)) x9 (.D(Data_in), .en(decoder_1_out9), .clk(Clk), .Q(x9_q), .clr(Reset));
  Register #(.trigger("falling"), .width(32)) x8 (.D(Data_in), .en(decoder_1_out8), .clk(Clk), .Q(x8_q), .clr(Reset));
  Register #(.trigger("falling"), .width(32)) x7 (.D(Data_in), .en(decoder_1_out7), .clk(Clk), .Q(x7_q), .clr(Reset));
  Register #(.trigger("falling"), .width(32)) x6 (.D(Data_in), .en(decoder_1_out6), .clk(Clk), .Q(x6_q), .clr(Reset));
  Register #(.trigger("falling"), .width(32)) x5 (.D(Data_in), .en(decoder_1_out5), .clk(Clk), .Q(x5_q), .clr(Reset));
  Register #(.trigger("falling"), .width(32)) x4 (.D(Data_in), .en(decoder_1_out4), .clk(Clk), .Q(x4_q), .clr(Reset));
  Register #(.trigger("falling"), .width(32)) x3 (.D(Data_in), .en(decoder_1_out3), .clk(Clk), .Q(x3_q), .clr(Reset));
  Register #(.trigger("falling"), .width(32)) x2 (.D(Data_in), .en(decoder_1_out2), .clk(Clk), .Q(x2_q), .clr(Reset));
  Register #(.trigger("falling"), .width(32)) x1 (.D(Data_in), .en(decoder_1_out1), .clk(Clk), .Q(x1_q), .clr(Reset));
  Multiplexer #(.select(5), .width(32)) multiplexer_1 (
    .in0({32{1'b0}}), .in1(x1_q), .in2(x2_q), .in3(x3_q), .in4(x4_q), .in5(x5_q), .in6(x6_q), .in7(x7_q),
    .in8(x8_q), .in9(x9_q), .in10(x10_q), .in11(x11_q), .in12(x12_q), .in13(x13_q), .in14(x14_q),
    .in15(x15_q), .in16(x16_q), .in17(x17_q), .in18(x18_q), .in19(x19_q), .in20(x20_q), .in21(x21_q),
    .in22(x22_q), .in23(x23_q), .in24(x24_q), .in25(x25_q), .in26(x26_q), .in27(x27_q), .in28(x28_q),
    .in29(x29_q), .in30(x30_q), .in31(x31_q), .out(Data_out2), .sel(Addr_out2));
  Multiplexer #(.select(5), .width(32)) multiplexer_2 (
    .in0({32{1'b0}}), .in1(x1_q), .in2(x2_q), .in3(x3_q), .in4(x4_q), .in5(x5_q), .in6(x6_q), .in7(x7_q),
    .in8(x8_q), .in9(x9_q), .in10(x10_q), .in11(x11_q), .in12(x12_q), .in13(x13_q), .in14(x14_q),
    .in15(x15_q), .in16(x16_q), .in17(x17_q), .in18(x18_q), .in19(x19_q), .in20(x20_q), .in21(x21_q),
    .in22(x22_q), .in23(x23_q), .in24(x24_q), .in25(x25_q), .in26(x26_q), .in27(x27_q), .in28(x28_q),
    .in29(x29_q), .in30(x30_q), .in31(x31_q), .out(Data_out1), .sel(Addr_out1));

  // Notes on the sheet:
  //   x0
endmodule

module ALU (
  input  [2:0] OpCode,
  input  [31:0] OP1,
  input  [31:0] OP2,
  output [31:0] S,
  output Zero
);

  wire [31:0] adder_1_out, and_1_out, or_1_out, shifter_1_out, shifter_2_out, subtractor_1_out, xor_1_out;

  Adder #(.width(32)) adder_1 (.a(OP1), .b(OP2), .out(adder_1_out));  // open: cin, cout
  Subtractor #(.width(32)) subtractor_1 (.a(OP1), .b(OP2), .out(subtractor_1_out));  // open: bin, bout
  assign xor_1_out = OP1 ^ OP2;  // XOR_Gate xor_1, 32 bits wide
  assign and_1_out = OP1 & OP2;  // AND_Gate and_1, 32 bits wide
  assign or_1_out = OP1 | OP2;  // OR_Gate or_1, 32 bits wide
  Shifter #(.shift("lr"), .width(32)) shifter_1 (.in(OP1), .\dist (OP2[4:0]), .out(shifter_1_out));
  Shifter #(.width(32)) shifter_2 (.in(OP1), .\dist (OP2[4:0]), .out(shifter_2_out));
  Multiplexer #(.select(3), .width(32)) multiplexer_1 (
    .in0({32{1'b0}}), .in1(adder_1_out), .in2(subtractor_1_out), .in3(xor_1_out), .in4(and_1_out),
    .in5(or_1_out), .in6(shifter_1_out), .in7(shifter_2_out), .out(S), .sel(OpCode));
  Comparator #(.mode("unsigned"), .width(32)) comparator_1 (.a(S), .b({32{1'b0}}), .eq(Zero));  // open: gt, lt
endmodule

module Program_Memory (
  input  Jmp,
  input  [7:0] Jmp_Offset,
  input  Clk,
  input  Rst,
  input  Stall,
  output [31:0] Instruction
);

  wire and_1_out, not_1_out, not_2_out, or_1_out;
  wire [7:0] adder_1_out, multiplexer_1_out, register_1_q;

  Register register_1 (.D(adder_1_out), .en(1'b1), .clk(and_1_out), .Q(register_1_q), .clr(Rst));
  Multiplexer #(.width(8)) multiplexer_1 (.in0({8{1'b0}}), .in1(Jmp_Offset), .out(multiplexer_1_out), .sel(Jmp));
  and and_1 (and_1_out, Clk, not_1_out);
  not not_1 (not_1_out, Stall);
  not not_2 (not_2_out, Jmp);
  or or_1 (or_1_out, and_1_out, Rst);
  RAM #(.dataWidth(32), .trigger("falling")) PROM (
    .addr(register_1_q), .we(1'b0), .oe(1'b1), .clk(or_1_out), .dout(Instruction));  // open: din
  Adder adder_1 (.a(multiplexer_1_out), .b(register_1_q), .out(adder_1_out), .cin(not_2_out));  // open: cout
endmodule

module Decode (
  input  [31:0] Instruction,
  input  Clk,
  input  Rst,
  output Jmp_Stall,
  output [8:0] Control_Lines,
  output [31:0] Imm,
  output [4:0] Addr_Out2,
  output [4:0] Addr_Out1,
  output [4:0] Addr_in
);

  wire not_1_out, not_2_out, or_1_out;
  wire [4:0] multiplexer_2_out;
  wire [8:0] multiplexer_3_out, pla_1_out;
  wire [11:0] multiplexer_1_out;
  wire [31:0] bit_extender_1_out;
  wire [46:0] multiplexer_4_out;

  PLA #(.in_width(32), .out_width(9), .\table ("0000000xxxxxxxxxx000xxxxx0110011 000000001 # ADD\nxxxxxxxxxxxxxxxxx000xxxxx0010011 000001001 # ADDI\n0100000xxxxxxxxxx000xxxxx0110011 000000010 # SUB\n0000000xxxxxxxxxx111xxxxx0110011 000000100 # AND\n0000000xxxxxxxxxx110xxxxx0110011 000000101 # OR\n0000000xxxxxxxxxx100xxxxx0110011 000000011 # XOR\nxxxxxxxxxxxxxxxxx010xxxxx0000011 000101001 # LW\nxxxxxxxxxxxxxxxxx010xxxxx0100011 001111001 # SW\nxxxxxxxxxxxxxxxxx000xxxxx1100011 111000010 # BEQ\nxxxxxxxxxxxxxxxxx001xxxxx1100011 011000010 # BNE\n0000000xxxxxxxxxx001xxxxx0110011 000000111 # SLL\n0000000xxxxxxxxxx101xxxxx0110011 000000110 # SRL")) pla_1 (
    .in(Instruction), .out({pla_1_out[8], Jmp_Stall, pla_1_out[6:0]}));
  not not_1 (not_1_out, pla_1_out[6]);
  or or_1 (or_1_out, pla_1_out[6], Jmp_Stall);
  Multiplexer #(.width(12)) multiplexer_1 (
    .in0({Instruction[31:25], Instruction[11:7]}), .in1(Instruction[31:20]), .out(multiplexer_1_out),
    .sel(not_1_out));
  Multiplexer #(.width(5)) multiplexer_2 (
    .in0(Instruction[11:7]), .in1({5{1'b0}}), .out(multiplexer_2_out), .sel(or_1_out));
  assign bit_extender_1_out = {{20{multiplexer_1_out[11]}}, multiplexer_1_out};  // Bit_Extender bit_extender_1
  not not_2 (not_2_out, Control_Lines[7]);
  Register #(.trigger("falling"), .width(9)) register_1 (
    .D(multiplexer_3_out), .en(1'b1), .clk(Clk), .Q(Control_Lines), .clr(Rst));
  Multiplexer #(.width(9)) multiplexer_3 (
    .in0({9{1'b0}}), .in1({pla_1_out[8], Jmp_Stall, pla_1_out[6:0]}), .out(multiplexer_3_out), .sel(not_2_out));
  Register #(.trigger("falling"), .width(47)) register_2 (
    .D(multiplexer_4_out), .en(1'b1), .clk(Clk), .Q({Addr_in, Addr_Out1, Addr_Out2, Imm}), .clr(Rst));
  Multiplexer #(.width(47)) multiplexer_4 (
    .in0({47{1'b0}}), .in1({multiplexer_2_out, Instruction[19:15], Instruction[24:20], bit_extender_1_out}),
    .out(multiplexer_4_out), .sel(not_2_out));
endmodule

module Data_Memory (
  input  [7:0] Addr,
  input  Enable,
  input  Read_Write,
  input  [31:0] Keyboard_In,
  input  [31:0] Data_In,
  input  Clk,
  input  Rst,
  output [31:0] Data_Out,
  output [15:0] Keyboard_Clr,
  output [63:0] Screen1,
  output [63:0] Screen2,
  output [63:0] Screen3,
  output [63:0] Screen4
);

  wire and_1_out, and_2_out, comparator_1_eq, comparator_2_eq, comparator_3_eq, decoder_1_out0,
       decoder_1_out1, decoder_1_out2, decoder_1_out3, decoder_1_out4, decoder_1_out5, decoder_1_out6,
       decoder_1_out7, decoder_1_out8, decoder_1_out9, decoder_1_out10, decoder_1_out11, decoder_1_out12,
       decoder_1_out13, decoder_1_out14, decoder_1_out15, not_1_out, not_2_out, or_1_out;
  wire [31:0] ram_1_dout;

  RAM #(.dataWidth(32)) ram_1 (
    .addr(Addr), .we(Read_Write), .oe(not_1_out), .clk(or_1_out), .din(Data_In), .dout(ram_1_dout));
  not not_1 (not_1_out, Read_Write);
  and and_1 (and_1_out, Clk, Enable);
  or or_1 (or_1_out, and_1_out, Rst);
  and and_2 (and_2_out, Read_Write, and_1_out);
  Comparator comparator_1 (.a(8'h11), .b(Addr), .eq(comparator_1_eq));  // open: gt, lt
  Comparator comparator_2 (.a(8'h10), .b(Addr), .eq(comparator_2_eq));  // open: gt, lt
  Comparator #(.mode("unsigned"), .width(4)) comparator_3 (
    .a(4'b0000), .b(Addr[7:4]), .eq(comparator_3_eq));  // open: gt, lt
  Decoder #(.select(4)) decoder_1 (
    .out0(decoder_1_out0), .out1(decoder_1_out1), .out2(decoder_1_out2), .out3(decoder_1_out3),
    .out4(decoder_1_out4), .out5(decoder_1_out5), .out6(decoder_1_out6), .out7(decoder_1_out7),
    .out8(decoder_1_out8), .out9(decoder_1_out9), .out10(decoder_1_out10), .out11(decoder_1_out11),
    .out12(decoder_1_out12), .out13(decoder_1_out13), .out14(decoder_1_out14), .out15(decoder_1_out15),
    .sel(Addr[3:0]), .en(comparator_3_eq));
  not not_2 (not_2_out, comparator_2_eq);
  Multiplexer #(.width(32)) multiplexer_1 (.in0(Keyboard_In), .in1(ram_1_dout), .out(Data_Out), .sel(not_2_out));
  Register #(.width(16)) register_1 (
    .D(Data_In[15:0]), .en(comparator_1_eq), .clk(and_2_out), .Q(Keyboard_Clr), .clr(Rst));
  Register #(.width(16)) register_2 (
    .D(Data_In[15:0]), .en(decoder_1_out15), .clk(and_2_out), .Q(Screen1[15:0]), .clr(Rst));
  Register #(.width(16)) register_3 (
    .D(Data_In[15:0]), .en(decoder_1_out14), .clk(and_2_out), .Q(Screen1[31:16]), .clr(Rst));
  Register #(.width(16)) register_4 (
    .D(Data_In[15:0]), .en(decoder_1_out13), .clk(and_2_out), .Q(Screen1[47:32]), .clr(Rst));
  Register #(.width(16)) register_5 (
    .D(Data_In[15:0]), .en(decoder_1_out12), .clk(and_2_out), .Q(Screen1[63:48]), .clr(Rst));
  Register #(.width(16)) register_6 (
    .D(Data_In[15:0]), .en(decoder_1_out11), .clk(and_2_out), .Q(Screen2[15:0]), .clr(Rst));
  Register #(.width(16)) register_7 (
    .D(Data_In[15:0]), .en(decoder_1_out10), .clk(and_2_out), .Q(Screen2[31:16]), .clr(Rst));
  Register #(.width(16)) register_8 (
    .D(Data_In[15:0]), .en(decoder_1_out9), .clk(and_2_out), .Q(Screen2[47:32]), .clr(Rst));
  Register #(.width(16)) register_9 (
    .D(Data_In[15:0]), .en(decoder_1_out8), .clk(and_2_out), .Q(Screen2[63:48]), .clr(Rst));
  Register #(.width(16)) register_10 (
    .D(Data_In[15:0]), .en(decoder_1_out7), .clk(and_2_out), .Q(Screen3[15:0]), .clr(Rst));
  Register #(.width(16)) register_11 (
    .D(Data_In[15:0]), .en(decoder_1_out6), .clk(and_2_out), .Q(Screen3[31:16]), .clr(Rst));
  Register #(.width(16)) register_12 (
    .D(Data_In[15:0]), .en(decoder_1_out5), .clk(and_2_out), .Q(Screen3[47:32]), .clr(Rst));
  Register #(.width(16)) register_13 (
    .D(Data_In[15:0]), .en(decoder_1_out4), .clk(and_2_out), .Q(Screen3[63:48]), .clr(Rst));
  Register #(.width(16)) register_14 (
    .D(Data_In[15:0]), .en(decoder_1_out3), .clk(and_2_out), .Q(Screen4[15:0]), .clr(Rst));
  Register #(.width(16)) register_15 (
    .D(Data_In[15:0]), .en(decoder_1_out2), .clk(and_2_out), .Q(Screen4[31:16]), .clr(Rst));
  Register #(.width(16)) register_16 (
    .D(Data_In[15:0]), .en(decoder_1_out1), .clk(and_2_out), .Q(Screen4[47:32]), .clr(Rst));
  Register #(.width(16)) register_17 (
    .D(Data_In[15:0]), .en(decoder_1_out0), .clk(and_2_out), .Q(Screen4[63:48]), .clr(Rst));
endmodule
